// Logisim project Lab_8.circ as structural Verilog: 1 circuit, main circuit main
module main (
  input  in_1,
  output [7:0] out_2
);

  wire CClock_out, undriven;
  wire [7:0] adder_1_out, register_1_q;

  Clock CClock (.out(CClock_out));
  Adder adder_1 (.a(register_1_q), .b(8'h1), .out(adder_1_out), .cin(undriven));  // open: cout
  Register register_1 (.D(adder_1_out), .en(in_1), .clk(CClock_out), .Q(register_1_q));  // open: clr
  RAM ram_1 (.addr(register_1_q), .we(1'b0), .oe(1'b1), .clk(CClock_out), .dout(out_2));  // open: din

  // Notes on the sheet:
  //   Harry Wang
  //   I pledge my honor that I have abided by the Stevens Honor System.
endmodule
